# Fritzing sketch booze-o-meter-schema (saved by Fritzing 0.9.3b)
breadboards: 1

parts:
  Part1 = Arduino Uno (Rev3)
  Q1 = NPN-Transistor [package="TO92 [THT]"]
  Q2 = NPN-Transistor [package="TO92 [THT]"]
  Q3 = NPN-Transistor [package="TO92 [THT]"]
  R1 = Resistor [tolerance=±5% resistance=10k package=THT]
  R2 = Resistor [tolerance=±5% resistance=10k package=THT]
  R3 = Resistor [tolerance=±5% resistance=10k package=THT]
  Part2 = sodaq mbili
  LED1 = smd LED [color="Red (633nm)" package="0603 [SMD]"]
  LED2 = smd LED [color="Yellow (595nm)" package="0603 [SMD]"]
  LED3 = smd LED [color="Green (570nm)" package="0603 [SMD]"]
  R4 = Resistor [tolerance=±5% resistance=220 package=THT]
  R5 = Resistor [tolerance=±5% resistance=220 package=THT]
  R6 = Resistor [tolerance=±5% resistance=220 package=THT]
  FLO-30_Circuit1 = FLO-30 Circuit
  FLO-30_Circuit2 = FLO-30 Circuit
  FLO-30_Circuit3 = FLO-30 Circuit

nets:
  N1: Part1.D8, FLO-30_Circuit1.PRB
  N2: Part1.D9_PWM, FLO-30_Circuit2.PRB
  N3: Part1.D10_PWM/SS, FLO-30_Circuit3.PRB
  N4: Part1.D11_PWM/MOSI, Q1.B
  N5: Part1.D12/MISO, Q2.B
  N6: Part1.D13/SCK, Q3.B
  N7: Part1.D2, R4.Pin_1
  N8: Part1.D3_PWM, R5.Pin_1
  N9: Part1.D4, R6.Pin_1
  VCC: Part1.5V, FLO-30_Circuit1.Vcc, FLO-30_Circuit2.Vcc, FLO-30_Circuit3.Vcc
  GND: Part1.GND, R1.Pin_1, R2.Pin_1, R3.Pin_1, Part2.GND, LED1.cathode, LED2.cathode, LED3.cathode, FLO-30_Circuit1.GND, FLO-30_Circuit2.GND, FLO-30_Circuit3.GND
  N10: Q1.E, Q2.E, Q3.E, Part2.3V3_SW
  N11: Q1.C, R3.Pin_0, Part2.D18
  N12: Q2.C, R2.Pin_0, Part2.D19
  N13: Q3.C, R1.Pin_0, Part2.D20
  N14: LED1.anode, R6.Pin_0
  N15: LED2.anode, R5.Pin_0
  N16: LED3.anode, R4.Pin_0
