# Fritzing sketch jax-demo-wiring (saved by Fritzing 0.9.1b)
breadboards: 1

parts:
  Part1 = Arduino Uno (Rev3)
  DHT1 = DHT22 Humidity and Temperature Sensor
  R1 = Resistor [tolerance=±5% resistance=4.7k package=THT]
  S1 = Momentary Switch [package=ksa_sealed_tac_switch]
  S2 = Momentary Switch [package=ksa_sealed_tac_switch]
  LED1 = smd LED [color="Red (633nm)" package="0805 [SMD]"]
  LED2 = smd LED [color="Red (633nm)" package="0805 [SMD]"]
  R2 = Resistor [tolerance=±5% resistance=220 package=THT]
  R3 = Resistor [tolerance=±5% resistance=220 package=THT]
  R4 = Resistor [tolerance=±5% resistance=10k package="0603 [SMD]"]
  R5 = Resistor [tolerance=±5% resistance=10k package="0603 [SMD]"]

nets:
  N1: Part1.D8, DHT1.DATA, R1.Pin_1
  GND: Part1.GND, DHT1.GND, LED1.cathode, LED2.cathode, R4.Pin_1, R5.Pin_1
  N2: Part1.D2, S2.1
  N3: Part1.D3_PWM, S1.1
  N4: Part1.D6_PWM, LED2.anode, R2.Pin_0
  N5: Part1.D7, LED1.anode, R3.Pin_0
  5V: Part1.5V, DHT1.VDD, R1.Pin_0, S1.4, S2.4
  N6: S1.2, R4.Pin_0
  N7: S2.2, R5.Pin_0
